// Logisim project Formula 1 Dasboard and control.circ as structural Verilog: 1 circuit, main circuit main
module main (
  input  [1:0] in_1,
  input  [6:0] in_2,
  input  Y,
  input  R,
  input  [2:0] in_5,
  input  in_6,
  input  [1:0] in_7,
  input  [1:0] in_8,
  input  [1:0] in_9,
  output [2:0] out_10
);

  wire and_1_out, and_2_out, and_3_out, and_4_out, and_5_out, and_6_out, and_7_out, and_8_out, and_9_out,
       and_10_out, and_11_out, and_12_out, bit_extender_1_out, bit_extender_3_out, button_1_out,
       button_2_out, button_3_out, button_4_out, clock_1_out, clock_2_out, comparator_1_eq, comparator_2_eq,
       comparator_2_gt, comparator_2_lt, comparator_3_eq, comparator_4_eq, comparator_5_eq, comparator_6_eq,
       comparator_6_lt, counter_1_q, counter_3_q, counter_7_q, counter_8_q, counter_9_q, counter_11_q,
       counter_12_q, counter_14_q, counter_15_q, counter_16_q, counter_17_q, counter_18_q, decoder_1_out1,
       decoder_2_out0, decoder_2_out1, decoder_2_out2, decoder_2_out3, decoder_2_out4, decoder_2_out5,
       decoder_2_out6, decoder_2_out7, decoder_3_out1, decoder_3_out2, decoder_3_out3, decoder_3_out4,
       decoder_3_out5, decoder_3_out6, decoder_3_out7, decoder_4_out0, decoder_4_out1, decoder_4_out2,
       decoder_4_out3, decoder_4_out4, decoder_4_out5, decoder_4_out6, decoder_4_out7, decoder_4_out8,
       decoder_4_out9, decoder_5_out1, decoder_6_out1, decoder_7_out0, decoder_7_out1, decoder_8_out0,
       decoder_8_out1, decoder_8_out2, decoder_8_out3, decoder_8_out4, decoder_8_out5, decoder_8_out6,
       decoder_8_out7, decoder_8_out8, decoder_8_out9, decoder_9_out1, decoder_10_out1, decoder_10_out2,
       decoder_10_out3, decoder_10_out4, decoder_10_out5, decoder_10_out7, decoder_11_out0, decoder_11_out1,
       decoder_11_out2, decoder_11_out3, decoder_11_out4, decoder_11_out5, decoder_11_out6, decoder_11_out7,
       decoder_11_out8, decoder_11_out9, multiplexer_1_out, multiplexer_2_out, nand_1_out, nand_2_out,
       nand_3_out, nand_4_out, nor_1_out, not_1_out, not_2_out, not_3_out, not_4_out, not_5_out, not_6_out,
       not_7_out, not_8_out, not_9_out, not_10_out, or_1_out, or_2_out, or_3_out, or_4_out, or_5_out,
       or_6_out, or_7_out, or_8_out, or_9_out, or_10_out, or_11_out, or_12_out, or_13_out, or_14_out,
       or_15_out, or_16_out, or_17_out, or_18_out, or_19_out, or_20_out, or_21_out, or_22_out, or_23_out,
       or_24_out, or_25_out, or_26_out, or_27_out, or_28_out, or_29_out, or_30_out, or_31_out, or_32_out,
       or_33_out, or_34_out, or_35_out, or_36_out, or_37_out, or_38_out, or_39_out, or_40_out, or_41_out,
       or_42_out, or_43_out, or_44_out, or_45_out, or_46_out, or_47_out, or_48_out, or_49_out, or_50_out,
       or_51_out, or_52_out, or_53_out, or_54_out, or_55_out, or_56_out, rom_2_data, rom_4_data;
  wire [1:0] bit_extender_4_out, bit_extender_5_out, bit_extender_6_out, bit_extender_7_out, counter_4_q,
       counter_6_q, multiplexer_4_out, multiplexer_5_out, rom_16_data, rom_22_data, rom_23_data;
  wire [2:0] multiplexer_3_out, rom_3_data, rom_6_data, rom_10_data, rom_39_data;
  wire [3:0] counter_13_q, rom_11_data, rom_24_data, rom_41_data;
  wire [4:0] counter_10_q, rom_25_data, rom_38_data, rom_40_data, rom_47_data, rom_53_data;
  wire [5:0] counter_2_q;
  wire [6:0] multiplexer_6_out, multiplexer_7_out, multiplexer_8_out, multiplexer_9_out, multiplexer_10_out,
       multiplexer_11_out, multiplexer_12_out, multiplexer_13_out, multiplexer_14_out, multiplexer_15_out,
       multiplexer_16_out, multiplexer_17_out, multiplexer_18_out, rom_12_data, rom_13_data, rom_14_data,
       rom_15_data, rom_17_data, rom_18_data, rom_19_data, rom_20_data, rom_26_data, rom_27_data,
       rom_28_data, rom_29_data, rom_30_data, rom_31_data, rom_32_data, rom_33_data, rom_34_data,
       rom_35_data, rom_36_data, rom_37_data, rom_42_data, rom_43_data, rom_44_data, rom_45_data,
       rom_46_data, rom_48_data, rom_49_data, rom_50_data, rom_51_data, rom_52_data, rom_54_data,
       rom_55_data, rom_56_data, rom_57_data, rom_58_data, rom_59_data, rom_60_data, rom_61_data, rom_62_data;
  wire [7:0] counter_5_q, counter_19_q, rom_1_data, rom_5_data, rom_7_data, rom_8_data, rom_9_data,
       rom_21_data;

  Counter #(.width(1), .max('h1)) counter_1 (
    .Q(counter_1_q), .clk(comparator_1_eq));  // open: load, D, count, carry, clr
  Comparator comparator_1 (.a(counter_5_q), .b(rom_1_data), .eq(comparator_1_eq));  // open: gt, lt
  ROM #(.addrWidth(3)) rom_1 (.addr(in_5), .data(rom_1_data));  // open: sel
  Decoder #(.enable("false")) decoder_1 (.out1(decoder_1_out1), .sel(counter_1_q));  // open: out0
  or or_1 (or_1_out, decoder_7_out0, not_1_out);
  or or_2 (or_2_out, rom_4_data, and_5_out);
  and and_1 (and_1_out, and_2_out, Y);
  and and_2 (and_2_out, decoder_7_out1, counter_3_q);
  nand nand_1 (nand_1_out, decoder_6_out1, comparator_2_eq);
  Counter #(.width(6), .max('h3f)) counter_2 (
    .Q(counter_2_q), .clk(and_1_out), .clr(not_2_out));  // open: load, D, count, carry
  and and_3 (and_3_out, decoder_7_out1, decoder_9_out1);
  not not_1 (not_1_out, decoder_9_out1);
  Bit_Extender #(.in_width(2), .out_width(1)) bit_extender_1 (.in(counter_6_q), .out(bit_extender_1_out));
  ROM #(.addrWidth(6), .dataWidth(1)) rom_2 (.addr(counter_2_q), .data(rom_2_data));  // open: sel
  or or_3 (or_3_out, R, decoder_6_out1, Y);
  or or_4 (or_4_out, rom_2_data, or_3_out);
  and and_4 (and_4_out, or_5_out, nand_3_out);
  Counter #(.width(1), .max('h1)) counter_3 (
    .count(1'b1), .Q(counter_3_q), .clk(multiplexer_2_out));  // open: load, D, carry, clr
  Counter #(.width(2), .max('h2)) counter_4 (
    .count(1'b1), .Q(counter_4_q), .clk(bit_extender_1_out), .clr(in_6));  // open: load, D, carry
  not not_2 (not_2_out, Y);
  or or_5 (or_5_out, or_4_out, and_8_out);
  nand nand_2 (nand_2_out, Y, comparator_2_eq);
  and and_5 (and_5_out, 1'b1, nand_2_out);
  Counter #(.max('h92)) counter_5 (
    .load(and_4_out), .D(rom_5_data), .count(or_2_out), .Q(counter_5_q), .clk(and_2_out), .clr(or_6_out));  // open: carry
  or or_6 (or_6_out, and_7_out, or_1_out, in_6);
  and and_6 (and_6_out, clock_1_out, nand_1_out, decoder_10_out7);
  Counter #(.width(2), .max('h2)) counter_6 (
    .count(1'b1), .Q(counter_6_q), .clk(and_6_out), .clr(in_6));  // open: load, D, carry
  Clock clock_1 (.out(clock_1_out));
  Multiplexer #(.enable("false")) multiplexer_1 (
    .in0(not_2_out), .in1(decoder_6_out1), .out(multiplexer_1_out), .sel(decoder_6_out1));
  and and_7 (and_7_out, R, decoder_2_out0);
  Decoder #(.select(3)) decoder_2 (
    .out0(decoder_2_out0), .out1(decoder_2_out1), .out2(decoder_2_out2), .out3(decoder_2_out3),
    .out4(decoder_2_out4), .out5(decoder_2_out5), .out6(decoder_2_out6), .out7(decoder_2_out7),
    .sel(rom_3_data), .en(and_3_out));
  ROM #(.dataWidth(3)) rom_3 (.addr(counter_5_q), .data(rom_3_data));  // open: sel
  ROM #(.addrWidth(6), .dataWidth(1)) rom_4 (.addr(counter_2_q), .data(rom_4_data));  // open: sel
  assign out_10 = {{2{multiplexer_1_out}}, multiplexer_1_out};  // Bit_Extender bit_extender_2
  Multiplexer #(.enable("false")) multiplexer_2 (
    .in0(bit_extender_3_out), .in1(counter_7_q), .out(multiplexer_2_out), .sel(decoder_5_out1));
  Bit_Extender #(.in_width(2), .out_width(1)) bit_extender_3 (.in(counter_4_q), .out(bit_extender_3_out));
  Counter #(.width(1), .max('h1)) counter_7 (
    .count(1'b1), .Q(counter_7_q), .clk(bit_extender_1_out));  // open: load, D, carry, clr
  or or_7 (or_7_out, decoder_2_out0, decoder_2_out1, decoder_2_out2, decoder_2_out3, decoder_2_out6, decoder_2_out7);
  and and_8 (and_8_out, Y, comparator_2_gt);
  Comparator comparator_2 (
    .a(counter_5_q), .b(rom_5_data), .gt(comparator_2_gt), .eq(comparator_2_eq), .lt(comparator_2_lt));
  ROM #(.addrWidth(3)) rom_5 (.addr(out_10), .data(rom_5_data));  // open: sel
  Multiplexer #(.width(3), .enable("false")) multiplexer_3 (
    .in0(rom_10_data), .in1(rom_6_data), .out(multiplexer_3_out), .sel(decoder_10_out7));
  ROM #(.dataWidth(3)) rom_6 (.addr(counter_5_q), .data(rom_6_data));  // open: sel
  or or_8 (or_8_out, decoder_2_out1, decoder_2_out2, decoder_2_out3, decoder_2_out4, decoder_2_out5, decoder_2_out7);
  nand nand_3 (nand_3_out, comparator_2_lt, Y);
  Decoder #(.select(3)) decoder_3 (
    .out1(decoder_3_out1), .out2(decoder_3_out2), .out3(decoder_3_out3), .out4(decoder_3_out4),
    .out5(decoder_3_out5), .out6(decoder_3_out6), .out7(decoder_3_out7), .sel(multiplexer_3_out),
    .en(decoder_9_out1));  // open: out0
  and and_9 (and_9_out, clock_1_out, decoder_9_out1, decoder_7_out1);
  Counter #(.width(1), .max('h1)) counter_8 (.Q(counter_8_q), .clk(clock_1_out));  // open: load, D, count, carry, clr
  Counter #(.width(1), .max('h1)) counter_9 (.Q(counter_9_q), .clk(counter_8_q));  // open: load, D, count, carry, clr
  or or_9 (or_9_out, decoder_2_out3, decoder_2_out4, decoder_2_out5, decoder_2_out7);
  or or_10 (or_10_out, decoder_2_out1, decoder_2_out2, decoder_2_out4, decoder_2_out5, decoder_2_out7, decoder_2_out6);
  or or_11 (or_11_out, decoder_2_out1, decoder_2_out2, decoder_2_out4, decoder_2_out5, decoder_2_out7);
  Counter #(.width(5), .max('h19)) counter_10 (
    .Q(counter_10_q), .clk(and_9_out), .clr(not_3_out));  // open: load, D, count, carry
  not not_3 (not_3_out, decoder_7_out1);
  Counter #(.width(1), .max('h1)) counter_11 (.Q(counter_11_q), .clk(counter_9_q));  // open: load, D, count, carry, clr
  Counter #(.width(1), .max('h1)) counter_12 (
    .Q(counter_12_q), .clk(counter_11_q));  // open: load, D, count, carry, clr
  not not_4 (not_4_out, decoder_2_out1);
  or or_12 (or_12_out, decoder_2_out1, decoder_2_out5, decoder_2_out7);
  or or_13 (or_13_out, decoder_3_out1, or_14_out);
  or or_14 (or_14_out, decoder_3_out2, or_15_out);
  or or_15 (or_15_out, decoder_3_out3, or_16_out);
  or or_16 (or_16_out, decoder_3_out4, or_17_out);
  ROM #(.addrWidth(2)) rom_7 (.addr(in_7), .data(rom_7_data));  // open: sel
  ROM #(.addrWidth(2)) rom_8 (.addr(in_8), .data(rom_8_data));  // open: sel
  ROM #(.addrWidth(2)) rom_9 (.addr(in_9), .data(rom_9_data));  // open: sel
  Comparator #(.mode("unsigned")) comparator_3 (
    .a(rom_9_data), .b(counter_19_q), .eq(comparator_3_eq));  // open: gt, lt
  or or_17 (or_17_out, decoder_3_out5, or_18_out);
  or or_18 (or_18_out, decoder_3_out6, decoder_3_out7);
  ROM #(.addrWidth(5), .dataWidth(3)) rom_10 (.addr(counter_10_q), .data(rom_10_data));  // open: sel
  ROM #(.dataWidth(4)) rom_11 (.addr(counter_5_q), .data(rom_11_data));  // open: sel
  Counter #(.width(4), .max('h9), .ongoal("stay")) counter_13 (
    .count(1'b1), .Q(counter_13_q), .clk(counter_12_q), .clr(not_5_out));  // open: load, D, carry
  not not_5 (not_5_out, decoder_6_out1);
  ROM #(.addrWidth(4), .dataWidth(7)) rom_12 (.addr(counter_13_q), .data(rom_12_data));  // open: sel
  ROM #(.addrWidth(4), .dataWidth(7)) rom_13 (.addr(counter_13_q), .data(rom_13_data));  // open: sel
  ROM #(.addrWidth(4), .dataWidth(7)) rom_14 (.addr(counter_13_q), .data(rom_14_data));  // open: sel
  ROM #(.addrWidth(4), .dataWidth(7)) rom_15 (.addr(counter_13_q), .data(rom_15_data));  // open: sel
  Decoder #(.select(4)) decoder_4 (
    .out0(decoder_4_out0), .out1(decoder_4_out1), .out2(decoder_4_out2), .out3(decoder_4_out3),
    .out4(decoder_4_out4), .out5(decoder_4_out5), .out6(decoder_4_out6), .out7(decoder_4_out7),
    .out8(decoder_4_out8), .out9(decoder_4_out9), .sel(rom_11_data), .en(decoder_9_out1));  // open: out10, out11, out12, out13, out14, out15
  Comparator #(.mode("unsigned")) comparator_4 (.a(counter_5_q), .b(rom_7_data), .eq(comparator_4_eq));  // open: gt, lt
  Comparator #(.mode("unsigned")) comparator_5 (.a(counter_5_q), .b(rom_8_data), .eq(comparator_5_eq));  // open: gt, lt
  or or_19 (or_19_out, decoder_4_out0, decoder_4_out9);
  not not_6 (not_6_out, comparator_4_eq);
  ROM #(.addrWidth(2), .dataWidth(2)) rom_16 (.addr(bit_extender_6_out), .data(rom_16_data));  // open: sel
  assign bit_extender_4_out = {{1{1'b0}}, comparator_3_eq};  // Bit_Extender bit_extender_4
  ROM #(.addrWidth(4), .dataWidth(7)) rom_17 (.addr(counter_13_q), .data(rom_17_data));  // open: sel
  ROM #(.addrWidth(4), .dataWidth(7)) rom_18 (.addr(counter_13_q), .data(rom_18_data));  // open: sel
  ROM #(.addrWidth(4), .dataWidth(7)) rom_19 (.addr(counter_13_q), .data(rom_19_data));  // open: sel
  ROM #(.addrWidth(4), .dataWidth(7)) rom_20 (.addr(counter_13_q), .data(rom_20_data));  // open: sel
  ROM #(.addrWidth(2)) rom_21 (.addr(in_1), .data(rom_21_data));  // open: sel
  or or_20 (or_20_out, decoder_4_out1, decoder_4_out2, decoder_4_out3, decoder_4_out4, decoder_4_out7, decoder_4_out8);
  or or_21 (or_21_out, or_19_out, or_20_out);
  assign bit_extender_5_out = {{1{1'b0}}, not_6_out};  // Bit_Extender bit_extender_5
  assign bit_extender_6_out = {{1{1'b0}}, comparator_5_eq};  // Bit_Extender bit_extender_6
  not not_7 (not_7_out, decoder_7_out1);
  Comparator comparator_6 (.a(rom_21_data), .b(counter_5_q), .eq(comparator_6_eq), .lt(comparator_6_lt));  // open: gt
  Counter #(.width(1), .max('h1)) counter_14 (
    .Q(counter_14_q), .clk(button_4_out), .clr(or_25_out));  // open: load, D, count, carry
  or or_22 (or_22_out, decoder_4_out2, decoder_4_out3, decoder_4_out4, decoder_4_out5, decoder_4_out6, decoder_4_out8);
  or or_23 (or_23_out, decoder_4_out4, decoder_4_out5, decoder_4_out6, decoder_4_out8);
  or or_24 (or_24_out, decoder_4_out2, decoder_4_out3, decoder_4_out5, decoder_4_out6, decoder_4_out8, decoder_4_out9, decoder_4_out0);
  Multiplexer #(.width(2), .enable("false")) multiplexer_4 (
    .in0(rom_23_data), .in1(rom_16_data), .out(multiplexer_4_out), .sel(comparator_5_eq));
  ROM #(.addrWidth(2), .dataWidth(2)) rom_22 (.addr(bit_extender_4_out), .data(rom_22_data));  // open: sel
  nand nand_4 (nand_4_out, not_7_out, decoder_9_out1);
  or or_25 (or_25_out, comparator_6_lt, comparator_6_eq);
  Decoder #(.enable("false")) decoder_5 (.out1(decoder_5_out1), .sel(counter_14_q));  // open: out0
  Counter #(.width(1), .max('h1)) counter_15 (
    .Q(counter_15_q), .clk(button_2_out));  // open: load, D, count, carry, clr
  Clock clock_2 (.out(clock_2_out));
  or or_26 (or_26_out, or_23_out, or_19_out);
  or or_27 (or_27_out, decoder_4_out2, decoder_4_out3, decoder_4_out5, decoder_4_out6, decoder_4_out8, decoder_4_out7);
  or or_28 (or_28_out, or_27_out, or_19_out);
  or or_29 (or_29_out, decoder_4_out2, decoder_4_out6, decoder_4_out0, decoder_4_out8);
  Multiplexer #(.width(2), .enable("false")) multiplexer_5 (
    .in0(multiplexer_4_out), .in1(rom_22_data), .out(multiplexer_5_out), .sel(comparator_3_eq));
  ROM #(.addrWidth(2), .dataWidth(2)) rom_23 (.addr(bit_extender_5_out), .data(rom_23_data));  // open: sel
  assign bit_extender_7_out = {{1{1'b0}}, nand_4_out};  // Bit_Extender bit_extender_7
  Decoder #(.enable("false")) decoder_6 (.out1(decoder_6_out1), .sel(counter_15_q));  // open: out0
  and and_10 (and_10_out, decoder_7_out1, decoder_9_out1, clock_2_out);
  not not_8 (not_8_out, decoder_4_out2);
  or or_30 (or_30_out, or_22_out, decoder_4_out9);
  ROM #(.dataWidth(4)) rom_24 (.addr(counter_5_q), .data(rom_24_data));  // open: sel
  ROM #(.addrWidth(2), .dataWidth(5)) rom_25 (.addr(bit_extender_7_out), .data(rom_25_data));  // open: sel
  Counter #(.width(1), .max('h1)) counter_16 (
    .Q(counter_16_q), .clk(button_1_out), .clr(R));  // open: load, D, count, carry
  Decoder #(.enable("false")) decoder_7 (.out0(decoder_7_out0), .out1(decoder_7_out1), .sel(counter_16_q));
  and and_11 (and_11_out, decoder_6_out1, clock_2_out);
  nor nor_1 (nor_1_out, R, Y);
  Decoder #(.select(4)) decoder_8 (
    .out0(decoder_8_out0), .out1(decoder_8_out1), .out2(decoder_8_out2), .out3(decoder_8_out3),
    .out4(decoder_8_out4), .out5(decoder_8_out5), .out6(decoder_8_out6), .out7(decoder_8_out7),
    .out8(decoder_8_out8), .out9(decoder_8_out9), .sel(rom_24_data), .en(decoder_9_out1));  // open: out10, out11, out12, out13, out14, out15
  Counter #(.width(1), .max('h1)) counter_17 (
    .load(decoder_5_out1), .Q(counter_17_q), .clk(button_3_out));  // open: D, count, carry, clr
  Counter #(.width(1), .max('h1)) counter_18 (.Q(counter_18_q), .clk(and_10_out));  // open: load, D, count, carry, clr
  Counter #(.ongoal("stay")) counter_19 (
    .Q(counter_19_q), .clk(counter_18_q), .clr(or_6_out));  // open: load, D, count, carry
  and and_12 (and_12_out, decoder_7_out1, nor_1_out);
  or or_31 (or_31_out, decoder_8_out0, decoder_8_out9);
  ROM #(.addrWidth(2), .dataWidth(7)) rom_26 (.addr(multiplexer_5_out), .data(rom_26_data));  // open: sel
  ROM #(.addrWidth(2), .dataWidth(7)) rom_27 (.addr(multiplexer_5_out), .data(rom_27_data));  // open: sel
  ROM #(.addrWidth(2), .dataWidth(7)) rom_28 (.addr(multiplexer_5_out), .data(rom_28_data));  // open: sel
  ROM #(.addrWidth(2), .dataWidth(7)) rom_29 (.addr(multiplexer_5_out), .data(rom_29_data));  // open: sel
  ROM #(.addrWidth(2), .dataWidth(7)) rom_30 (.addr(multiplexer_5_out), .data(rom_30_data));  // open: sel
  ROM #(.addrWidth(2), .dataWidth(7)) rom_31 (.addr(multiplexer_5_out), .data(rom_31_data));  // open: sel
  ROM #(.addrWidth(2), .dataWidth(7)) rom_32 (.addr(multiplexer_5_out), .data(rom_32_data));  // open: sel
  ROM #(.addrWidth(2), .dataWidth(7)) rom_33 (.addr(multiplexer_5_out), .data(rom_33_data));  // open: sel
  ROM #(.addrWidth(2), .dataWidth(7)) rom_34 (.addr(multiplexer_5_out), .data(rom_34_data));  // open: sel
  ROM #(.addrWidth(2), .dataWidth(7)) rom_35 (.addr(multiplexer_5_out), .data(rom_35_data));  // open: sel
  ROM #(.addrWidth(2), .dataWidth(7)) rom_36 (.addr(multiplexer_5_out), .data(rom_36_data));  // open: sel
  ROM #(.addrWidth(2), .dataWidth(7)) rom_37 (.addr(multiplexer_5_out), .data(rom_37_data));  // open: sel
  ROM #(.addrWidth(2), .dataWidth(5)) rom_38 (.addr(bit_extender_7_out), .data(rom_38_data));  // open: sel
  Decoder #(.enable("false")) decoder_9 (.out1(decoder_9_out1), .sel(counter_17_q));  // open: out0
  LED led_1 (.in(or_13_out));
  LED led_2 (.in(decoder_9_out1));
  or or_32 (or_32_out, decoder_8_out1, decoder_8_out2, decoder_8_out3, decoder_8_out4, decoder_8_out7, decoder_8_out8);
  or or_33 (or_33_out, or_31_out, or_32_out);
  Multiplexer #(.width(7), .enable("false")) multiplexer_6 (
    .in0(rom_30_data), .in1(rom_17_data), .out(multiplexer_6_out), .sel(decoder_6_out1));
  Multiplexer #(.width(7), .enable("false")) multiplexer_7 (
    .in0(rom_31_data), .in1(rom_18_data), .out(multiplexer_7_out), .sel(decoder_6_out1));
  Multiplexer #(.width(7), .enable("false")) multiplexer_8 (
    .in0(rom_32_data), .in1(rom_19_data), .out(multiplexer_8_out), .sel(decoder_6_out1));
  Multiplexer #(.width(7), .enable("false")) multiplexer_9 (
    .in0(rom_33_data), .in1(rom_20_data), .out(multiplexer_9_out), .sel(decoder_6_out1));
  Multiplexer #(.width(7), .enable("false")) multiplexer_10 (
    .in0(rom_34_data), .in1(rom_12_data), .out(multiplexer_10_out), .sel(decoder_6_out1));
  Multiplexer #(.width(7), .enable("false")) multiplexer_11 (
    .in0(rom_35_data), .in1(rom_13_data), .out(multiplexer_11_out), .sel(decoder_6_out1));
  Multiplexer #(.width(7), .enable("false")) multiplexer_12 (
    .in0(rom_36_data), .in1(rom_14_data), .out(multiplexer_12_out), .sel(decoder_6_out1));
  Multiplexer #(.width(7), .enable("false")) multiplexer_13 (
    .in0(rom_37_data), .in1(rom_15_data), .out(multiplexer_13_out), .sel(decoder_6_out1));
  Decoder #(.select(3)) decoder_10 (
    .out1(decoder_10_out1), .out2(decoder_10_out2), .out3(decoder_10_out3), .out4(decoder_10_out4),
    .out5(decoder_10_out5), .out7(decoder_10_out7), .sel(rom_39_data), .en(decoder_9_out1));  // open: out0, out6
  LED led_3 (.in(and_12_out));
  LED led_4 (.in(Y));
  LED led_5 (.in(R));
  _7_Segment_Display u_7_segment_display_1 (
    .g(or_8_out), .f(or_9_out), .a(or_10_out), .b(or_7_out), .e(or_12_out), .d(or_11_out), .c(not_4_out));  // open: dp
  LED led_6 (.in(or_17_out));
  LED led_7 (.in(or_14_out));
  LED led_8 (.in(or_16_out));
  LED led_9 (.in(or_15_out));
  or or_34 (or_34_out, decoder_8_out2, decoder_8_out3, decoder_8_out4, decoder_8_out5, decoder_8_out6, decoder_8_out8);
  or or_35 (or_35_out, decoder_8_out4, decoder_8_out5, decoder_8_out6, decoder_8_out8);
  or or_36 (or_36_out, decoder_8_out2, decoder_8_out3, decoder_8_out5, decoder_8_out6, decoder_8_out8, decoder_8_out9, decoder_8_out0);
  ROM #(.dataWidth(3)) rom_39 (.addr(counter_19_q), .data(rom_39_data));  // open: sel
  Button button_1 (.out(button_1_out));
  LED led_10 (.in(or_41_out));
  Button button_2 (.out(button_2_out));
  LED led_11 (.in(and_11_out));
  Button button_3 (.out(button_3_out));
  LED led_12 (.in(or_18_out));
  LED led_13 (.in(decoder_3_out7));
  _7_Segment_Display u_7_segment_display_2 (
    .g(or_30_out), .f(or_26_out), .a(or_28_out), .b(or_21_out), .e(or_29_out), .d(or_24_out), .c(not_8_out));  // open: dp
  or or_37 (or_37_out, or_35_out, or_31_out);
  or or_38 (or_38_out, decoder_8_out2, decoder_8_out3, decoder_8_out5, decoder_8_out6, decoder_8_out8, decoder_8_out7);
  or or_39 (or_39_out, or_38_out, or_31_out);
  or or_40 (or_40_out, decoder_8_out2, decoder_8_out6, decoder_8_out0, decoder_8_out8);
  ROM #(.addrWidth(2), .dataWidth(5)) rom_40 (.addr(bit_extender_7_out), .data(rom_40_data));  // open: sel
  or or_41 (or_41_out, decoder_10_out1, or_42_out);
  or or_42 (or_42_out, decoder_10_out2, or_44_out);
  LED led_14 (.in(or_44_out));
  LED led_15 (.in(or_42_out));
  LED led_16 (.in(or_45_out));
  _7_Segment_Display u_7_segment_display_3 (
    .g(or_43_out), .f(or_37_out), .a(or_39_out), .b(or_33_out), .e(or_40_out), .d(or_36_out), .c(not_9_out));  // open: dp
  not not_9 (not_9_out, decoder_8_out2);
  or or_43 (or_43_out, or_34_out, decoder_8_out9);
  ROM #(.dataWidth(4)) rom_41 (.addr(counter_5_q), .data(rom_41_data));  // open: sel
  ROM #(.addrWidth(4), .dataWidth(7)) rom_42 (.addr(counter_13_q), .data(rom_42_data));  // open: sel
  ROM #(.addrWidth(4), .dataWidth(7)) rom_43 (.addr(counter_13_q), .data(rom_43_data));  // open: sel
  ROM #(.addrWidth(4), .dataWidth(7)) rom_44 (.addr(counter_13_q), .data(rom_44_data));  // open: sel
  ROM #(.addrWidth(4), .dataWidth(7)) rom_45 (.addr(counter_13_q), .data(rom_45_data));  // open: sel
  ROM #(.addrWidth(4), .dataWidth(7)) rom_46 (.addr(counter_13_q), .data(rom_46_data));  // open: sel
  or or_44 (or_44_out, decoder_10_out3, or_45_out);
  or or_45 (or_45_out, decoder_10_out4, decoder_10_out5);
  LED led_17 (.in(decoder_10_out5));
  DotMatrix #(.matrixrows(5)) dotmatrix_1 (
    .col0(rom_25_data), .col1(rom_38_data), .col2(rom_40_data), .col3(rom_47_data), .col4(rom_53_data));
  LED led_18 (.in(decoder_5_out1));
  Button button_4 (.out(button_4_out));
  _7_Segment_Display u_7_segment_display_4 (
    .g(or_54_out), .f(or_51_out), .a(or_55_out), .b(or_48_out), .e(or_56_out), .d(or_53_out), .c(not_10_out));  // open: dp
  Decoder #(.select(4)) decoder_11 (
    .out0(decoder_11_out0), .out1(decoder_11_out1), .out2(decoder_11_out2), .out3(decoder_11_out3),
    .out4(decoder_11_out4), .out5(decoder_11_out5), .out6(decoder_11_out6), .out7(decoder_11_out7),
    .out8(decoder_11_out8), .out9(decoder_11_out9), .sel(rom_41_data), .en(decoder_9_out1));  // open: out10, out11, out12, out13, out14, out15
  Multiplexer #(.width(7), .enable("false")) multiplexer_14 (
    .in0(rom_48_data), .in1(rom_42_data), .out(multiplexer_14_out), .sel(decoder_6_out1));
  Multiplexer #(.width(7), .enable("false")) multiplexer_15 (
    .in0(rom_49_data), .in1(rom_43_data), .out(multiplexer_15_out), .sel(decoder_6_out1));
  Multiplexer #(.width(7), .enable("false")) multiplexer_16 (
    .in0(rom_50_data), .in1(rom_44_data), .out(multiplexer_16_out), .sel(decoder_6_out1));
  Multiplexer #(.width(7), .enable("false")) multiplexer_17 (
    .in0(rom_51_data), .in1(rom_45_data), .out(multiplexer_17_out), .sel(decoder_6_out1));
  Multiplexer #(.width(7), .enable("false")) multiplexer_18 (
    .in0(rom_52_data), .in1(rom_46_data), .out(multiplexer_18_out), .sel(decoder_6_out1));
  ROM #(.addrWidth(2), .dataWidth(5)) rom_47 (.addr(bit_extender_7_out), .data(rom_47_data));  // open: sel
  DotMatrix #(.matrixcols(27), .persist(60)) dotmatrix_2 (
    .col0(rom_26_data), .col1(rom_27_data), .col2(rom_28_data), .col3(rom_29_data), .col4(in_2),
    .col5(multiplexer_6_out), .col6(multiplexer_7_out), .col7(multiplexer_8_out), .col8(multiplexer_9_out),
    .col9(in_2), .col10(multiplexer_10_out), .col11(multiplexer_11_out), .col12(multiplexer_12_out),
    .col13(multiplexer_13_out), .col14(in_2), .col15(multiplexer_14_out), .col16(multiplexer_15_out),
    .col17(multiplexer_16_out), .col18(multiplexer_17_out), .col19(multiplexer_18_out), .col20(in_2),
    .col21(rom_54_data), .col22(in_2), .col23(rom_59_data), .col24(rom_60_data), .col25(rom_61_data),
    .col26(rom_62_data));
  DotMatrix #(.persist(60)) dotmatrix_3 (
    .col0(rom_55_data), .col1(rom_56_data), .col2(rom_57_data), .col3(rom_58_data), .col4(in_2));
  ROM #(.addrWidth(2), .dataWidth(7)) rom_48 (.addr(multiplexer_5_out), .data(rom_48_data));  // open: sel
  ROM #(.addrWidth(2), .dataWidth(7)) rom_49 (.addr(multiplexer_5_out), .data(rom_49_data));  // open: sel
  ROM #(.addrWidth(2), .dataWidth(7)) rom_50 (.addr(multiplexer_5_out), .data(rom_50_data));  // open: sel
  ROM #(.addrWidth(2), .dataWidth(7)) rom_51 (.addr(multiplexer_5_out), .data(rom_51_data));  // open: sel
  ROM #(.addrWidth(2), .dataWidth(7)) rom_52 (.addr(multiplexer_5_out), .data(rom_52_data));  // open: sel
  or or_46 (or_46_out, decoder_11_out1, decoder_11_out2, decoder_11_out3, decoder_11_out4, decoder_11_out7, decoder_11_out8);
  or or_47 (or_47_out, decoder_11_out0, decoder_11_out9);
  or or_48 (or_48_out, or_47_out, or_46_out);
  ROM #(.addrWidth(2), .dataWidth(5)) rom_53 (.addr(bit_extender_7_out), .data(rom_53_data));  // open: sel
  or or_49 (or_49_out, decoder_11_out2, decoder_11_out3, decoder_11_out4, decoder_11_out5, decoder_11_out6, decoder_11_out8);
  ROM #(.addrWidth(2), .dataWidth(7)) rom_54 (.addr(multiplexer_5_out), .data(rom_54_data));  // open: sel
  ROM #(.addrWidth(2), .dataWidth(7)) rom_55 (.addr(multiplexer_5_out), .data(rom_55_data));  // open: sel
  ROM #(.addrWidth(2), .dataWidth(7)) rom_56 (.addr(multiplexer_5_out), .data(rom_56_data));  // open: sel
  ROM #(.addrWidth(2), .dataWidth(7)) rom_57 (.addr(multiplexer_5_out), .data(rom_57_data));  // open: sel
  ROM #(.addrWidth(2), .dataWidth(7)) rom_58 (.addr(multiplexer_5_out), .data(rom_58_data));  // open: sel
  or or_50 (or_50_out, decoder_11_out4, decoder_11_out5, decoder_11_out6, decoder_11_out8);
  or or_51 (or_51_out, or_50_out, or_47_out);
  or or_52 (or_52_out, decoder_11_out2, decoder_11_out3, decoder_11_out5, decoder_11_out6, decoder_11_out8, decoder_11_out7);
  or or_53 (or_53_out, decoder_11_out2, decoder_11_out3, decoder_11_out5, decoder_11_out6, decoder_11_out8, decoder_11_out9, decoder_11_out0);
  or or_54 (or_54_out, or_49_out, decoder_11_out9);
  or or_55 (or_55_out, or_52_out, or_47_out);
  or or_56 (or_56_out, decoder_11_out2, decoder_11_out6, decoder_11_out0, decoder_11_out8);
  not not_10 (not_10_out, decoder_11_out2);
  ROM #(.addrWidth(2), .dataWidth(7)) rom_59 (.addr(multiplexer_5_out), .data(rom_59_data));  // open: sel
  ROM #(.addrWidth(2), .dataWidth(7)) rom_60 (.addr(multiplexer_5_out), .data(rom_60_data));  // open: sel
  ROM #(.addrWidth(2), .dataWidth(7)) rom_61 (.addr(multiplexer_5_out), .data(rom_61_data));  // open: sel
  ROM #(.addrWidth(2), .dataWidth(7)) rom_62 (.addr(multiplexer_5_out), .data(rom_62_data));  // open: sel

  // Notes on the sheet:
  //   contents of rom_1 (hex, n*v repeats v):
  //   d
  //   contents of rom_2 (hex, n*v repeats v):
  //   4*0 1 1 0 1 4*0 1 0 0 1 1 8*0 1 1 11*0 1 1 6*0 1 1 0 0 0 1 5*0 1 4*0 1
  //   contents of rom_3 (hex, n*v repeats v):
  //   5*0 7*1 9*2 10*3 12*4 15*5 24*6 38*7 6 6 6 5 5 5 4 4 4 3 3 3 2 2 2 1 1 1
  //   contents of rom_4 (hex, n*v repeats v):
  //   13*1 0 0 1 1 0 0 1 1 0 1 1 0 1 1 1 0 0 1 1 0 1 0 0 4*1 0 1 4*0 1 1 0 1 0 1 1 1 0 1 0 1 0 1 0 0 1 1
  //   contents of rom_5 (hex, n*v repeats v):
  //   d ff 5*0 7
  //   contents of rom_6 (hex, n*v repeats v):
  //   1 1 2 4 7 0 1 2 3 4 5 7 0 1 2 3 4 5 6 6 7 0 1 2 3 4 5 5 6 6 7 0 1 2 3 3 4 4 5 5 6 6 7 0 1 2 2 3 3 4
  //   4 5 5 5 6 6 6 7 0 1 1 2 2 3 3 4*4 5*5 5*6 7 7 7 0 0 1 1 1 4*2 5*3 5*4 5*5 7*6 6*7 0 7 6 0 7 6 0 7 6
  //   0 7 6 0 7 6 0 7 6 0 7 6 0 0 7*1
  //   contents of rom_7 (hex, n*v repeats v):
  //   70
  //   contents of rom_8 (hex, n*v repeats v):
  //   76
  //   contents of rom_9 (hex, n*v repeats v):
  //   fc
  //   contents of rom_10 (hex, n*v repeats v):
  //   1 1 2 2 3 3 4 4 5 5 6 6 7 7 6 6 5 5 4 4 3 3 2 2 1
  //   contents of rom_11 (hex, n*v repeats v):
  //   10*0 22*1 47*2 41*3 4*2 6*1
  //   contents of rom_12 (hex, n*v repeats v):
  //   7f 0 0 0 7f 0 0 0 7f
  //   contents of rom_13 (hex, n*v repeats v):
  //   41 0 0 0 41 0 0 0 41
  //   contents of rom_14 (hex, n*v repeats v):
  //   41 0 0 0 41 0 0 0 41
  //   contents of rom_15 (hex, n*v repeats v):
  //   7f 0 0 0 7f 0 0 0 7f
  //   contents of rom_16 (hex, n*v repeats v):
  //   1 3 1 1
  //   contents of rom_17 (hex, n*v repeats v):
  //   7f 0 0 0 7f 0 0 0 7f
  //   contents of rom_18 (hex, n*v repeats v):
  //   49 0 0 0 49 0 0 0 49
  //   contents of rom_19 (hex, n*v repeats v):
  //   55 0 0 0 55 0 0 0 55
  //   contents of rom_20 (hex, n*v repeats v):
  //   63 0 0 0 63 0 0 0 63
  //   contents of rom_21 (hex, n*v repeats v):
  //   78
  //   contents of rom_22 (hex, n*v repeats v):
  //   1 2 1 1
  //   contents of rom_23 (hex, n*v repeats v):
  //   0 1 1 1
  //   contents of rom_24 (hex, n*v repeats v):
  //   0 0 1 2 3 4 5 6 8 9 0 0 1 1 2 2 3 3 4 4 5 5 6 6 7 7 8 8 8 9 9 9 4*0 1 1 1 6*2 6*3 5*4 5*5 6*6 4*7
  //   4*8 4*9 0 0 0 7*1 8*2 23*3 8 5 3 0 9 7 4 3 1 0 9 7 5 2
  //   contents of rom_25 (hex, n*v repeats v):
  //   1f
  //   contents of rom_26 (hex, n*v repeats v):
  //   7f 0 7f 3f
  //   contents of rom_27 (hex, n*v repeats v):
  //   41 0 48 48
  //   contents of rom_28 (hex, n*v repeats v):
  //   49 0 48 48
  //   contents of rom_29 (hex, n*v repeats v):
  //   4f 0 40 3f
  //   contents of rom_30 (hex, n*v repeats v):
  //   7f 0 7f 7f
  //   contents of rom_31 (hex, n*v repeats v):
  //   4c 0 48 41
  //   contents of rom_32 (hex, n*v repeats v):
  //   4a 0 48 49
  //   contents of rom_33 (hex, n*v repeats v):
  //   79 0 40 4f
  //   contents of rom_34 (hex, n*v repeats v):
  //   3f 0 7e 3f
  //   contents of rom_35 (hex, n*v repeats v):
  //   48 0 3 48
  //   contents of rom_36 (hex, n*v repeats v):
  //   48 0 3 48
  //   contents of rom_37 (hex, n*v repeats v):
  //   3f 0 7e 3f
  //   contents of rom_38 (hex, n*v repeats v):
  //   8
  //   FLAG
  //   G
  //   contents of rom_39 (hex, n*v repeats v):
  //   0 47*1 48*2 48*3 48*4 54*5 6*6 4*7
  //   PIT
  //   FIRE
  //   ENGINE
  //   contents of rom_40 (hex, n*v repeats v):
  //   4
  //   contents of rom_41 (hex, n*v repeats v):
  //   0 8 4 5 1 8 2 0 4 7 1 9 3 8 4 9 7 8 1 7 4 9 2 7 5 8 2 7 9 3 6 9 1 2 5 8 3 4 9 1 4 5 7 8 9 0 3 4 7 7
  //   8 0 1 2 5 8 1 2 3 7 8 0 2 3 5 6 9 0 3 6 7 1 4 7 9 0 1 2 5 1 3 8 1 2 3 5 7 8 9 1 2 3 4 5 6 7 9 0 0 1
  //   1 2 2 2 3 3 3 4 4 4 5 5 5 6 6 6 4*7 4*3 7*2
  //   contents of rom_42 (hex, n*v repeats v):
  //   63 0 0 0 63 0 0 0 63
  //   contents of rom_43 (hex, n*v repeats v):
  //   14 0 0 0 14 0 0 0 14
  //   contents of rom_44 (hex, n*v repeats v):
  //   8 0 0 0 8 0 0 0 8
  //   contents of rom_45 (hex, n*v repeats v):
  //   14 0 0 0 14 0 0 0 14
  //   contents of rom_46 (hex, n*v repeats v):
  //   63 0 0 0 63 0 0 0 63
  //   DRS
  //   OVERTAKE
  //   contents of rom_47 (hex, n*v repeats v):
  //   2
  //   KPH
  //   contents of rom_48 (hex, n*v repeats v):
  //   43 0 7f 43
  //   contents of rom_49 (hex, n*v repeats v):
  //   45 0 41 45
  //   contents of rom_50 (hex, n*v repeats v):
  //   49 0 49 49
  //   contents of rom_51 (hex, n*v repeats v):
  //   51 0 4f 51
  //   contents of rom_52 (hex, n*v repeats v):
  //   61 0 0 61
  //   contents of rom_53 (hex, n*v repeats v):
  //   1f
  //   contents of rom_54 (hex, n*v repeats v):
  //   7f 0 0 7f
  //   contents of rom_55 (hex, n*v repeats v):
  //   0 0 7f 7f
  //   contents of rom_56 (hex, n*v repeats v):
  //   0 0 41 4c
  //   contents of rom_57 (hex, n*v repeats v):
  //   0 0 41 4a
  //   contents of rom_58 (hex, n*v repeats v):
  //   0 0 7f 79
  //   contents of rom_59 (hex, n*v repeats v):
  //   7f 0 7f
  //   contents of rom_60 (hex, n*v repeats v):
  //   49 0 41
  //   contents of rom_61 (hex, n*v repeats v):
  //   49 0 41
  //   contents of rom_62 (hex, n*v repeats v):
  //   49 0 7f
endmodule
